// Logisim project Proje.circ as structural Verilog: 8 circuits, main circuit CPU
module CPU (
  input  Clear_PC
);

  wire and_1_out, CF, ChangePC, Clock, CompareSignal, dataMemRead,
       jump_condition_checker_1_jumpconditionresult, jumpCondCheck, JumpConditionResult, loadData, memWrite,
       multiplexer_1_out, PCWrite, regWrite, ZF;
  wire [1:0] control_unit_1_alucontrol;
  wire [2:0] JumpSignal;
  wire [3:0] OpCode, RealSource1;
  wire [11:0] _12Bit_Address_Count, adder_1_out, DataStoreAddress, multiplexer_2_out, PCValue;
  wire [15:0] AluResult, DataMemory, multiplexer_4_out, Reg1, Reg2;

  Jump_Condition_Checker jump_condition_checker_1 (
    .jumpCondCheck(jumpCondCheck), .JumpSignal(JumpSignal), .ZF(ZF), .CF(CF),
    .JumpConditionResult(jump_condition_checker_1_jumpconditionresult));
  Multiplexer #(.enable("false")) multiplexer_1 (
    .in0(1'b0), .in1(JumpConditionResult), .out(multiplexer_1_out), .sel(ChangePC));
  or or_1 (JumpConditionResult, jump_condition_checker_1_jumpconditionresult, ~OpCode[3]);  // OR_Gate
  Multiplexer #(.width(12), .enable("false")) multiplexer_2 (
    .in0(12'h1), .in1(_12Bit_Address_Count), .out(multiplexer_2_out), .sel(multiplexer_1_out));
  Adder_part #(.width(12)) adder_1 (.a(PCValue), .b(multiplexer_2_out), .out(adder_1_out), .cin(1'b0));  // open: cout
  Register #(.width(12)) PC (.D(adder_1_out), .en(PCWrite), .Q(PCValue), .clk(Clock), .clr(Clear_PC));
  Clock u_Clock (.out(Clock));
  and and_1 (and_1_out, ~OpCode[0], OpCode[1], OpCode[2], ~OpCode[3]);  // AND_Gate
  ROM #(.addrWidth(12), .dataWidth(16)) rom_1 (.addr(PCValue), .data({OpCode, _12Bit_Address_Count}), .sel(1'b1));
  Multiplexer #(.width(4), .enable("false")) multiplexer_3 (
    .in0(_12Bit_Address_Count[7:4]), .in1(_12Bit_Address_Count[11:8]), .out(RealSource1), .sel(and_1_out));
  assign DataStoreAddress = {{4{1'b0}}, _12Bit_Address_Count[7:0]};  // Bit_Extender bit_extender_1
  Multiplexer #(.width(16), .enable("false")) multiplexer_4 (
    .in0(DataMemory), .in1(AluResult), .out(multiplexer_4_out), .sel(loadData));
  Control_Unit control_unit_1 (
    .Op_Code(OpCode), .ChangePC(ChangePC), .PCWrite(PCWrite), .ALUControl(control_unit_1_alucontrol),
    .memWrite(memWrite), .Clock(Clock), .regWrite(regWrite), .dataMemRead(dataMemRead), .loadData(loadData),
    .CompareSignal(CompareSignal), .JumpSignal(JumpSignal), .jumpCondCheck(jumpCondCheck));  // open: PCReadSignal, InstReadSignal
  Register_File register_file_1 (
    .Data_to_Write(multiplexer_4_out), .Write_to_Register(regWrite), .OUTPUT_A___SELECTOR(RealSource1),
    .Register_to_Write(_12Bit_Address_Count[11:8]), .OUTPUT_B___SELECTOR(_12Bit_Address_Count[3:0]),
    .CLK(Clock), .OUTPUT_A(Reg1), .OUTPUT_B(Reg2));
  ALU alu_1 (
    .Src_A(Reg1), .Src_B(Reg2), .IMM(_12Bit_Address_Count[3:0]), .Alu_Control(control_unit_1_alucontrol),
    .Result(AluResult));
  Comparator comparator_1 (
    .Number_A(Reg1), .Number_B(Reg2), .ZF(ZF), .CF(CF), .ComparatorSignal(CompareSignal), .Clock(Clock));
  RAM #(.addrWidth(12), .dataWidth(16), .bus("separate")) ram_1 (
    .addr(DataStoreAddress), .din(Reg1), .data(DataMemory), .str(memWrite), .sel(1'b1), .clk(Clock),
    .ld(dataMemRead));  // open: clr

  // Other names for the same wires on the sheet: Source1[3:0] = _12Bit_Address_Count[7:4];
  //   Destination[3:0] = _12Bit_Address_Count[11:8]

  // Notes on the sheet:
  //   INSTRUCTION MEMORY
  //   contents of rom_1 (hex, n*v repeats v):
  //   7005
  //   DATA MEMORY
endmodule

// REGISTER FILE
module Register_File (
  input  [15:0] Data_to_Write,
  input  Write_to_Register,
  input  [3:0] OUTPUT_A___SELECTOR,
  input  [3:0] Register_to_Write,
  input  [3:0] OUTPUT_B___SELECTOR,
  input  CLK,
  output [15:0] OUTPUT_A,
  output [15:0] OUTPUT_B
);

  wire and_1_out, and_2_out, and_3_out, and_4_out, and_5_out, and_6_out, and_7_out, and_8_out, and_9_out,
       and_10_out, and_11_out, and_12_out, and_13_out, and_14_out, and_15_out, and_16_out, decoder_1_out0,
       decoder_1_out1, decoder_1_out2, decoder_1_out3, decoder_1_out4, decoder_1_out5, decoder_1_out6,
       decoder_1_out7, decoder_1_out8, decoder_1_out9, decoder_1_out10, decoder_1_out11, decoder_1_out12,
       decoder_1_out13, decoder_1_out14, decoder_1_out15;
  wire [15:0] R0_q, R1_q, R2_q, R3_q, R4_q, R5_q, R6_q, R7_q, R8_q, R9_q, R10_q, R11_q, R12_q, R13_q, R14_q,
       R15_q;

  Decoder #(.select(4), .enable("false")) decoder_1 (
    .out0(decoder_1_out0), .out1(decoder_1_out1), .out2(decoder_1_out2), .out3(decoder_1_out3),
    .out4(decoder_1_out4), .out5(decoder_1_out5), .out6(decoder_1_out6), .out7(decoder_1_out7),
    .out8(decoder_1_out8), .out9(decoder_1_out9), .out10(decoder_1_out10), .out11(decoder_1_out11),
    .out12(decoder_1_out12), .out13(decoder_1_out13), .out14(decoder_1_out14), .out15(decoder_1_out15),
    .sel(Register_to_Write));
  and and_1 (and_1_out, Write_to_Register, decoder_1_out0);
  and and_2 (and_2_out, Write_to_Register, decoder_1_out1);
  and and_3 (and_3_out, Write_to_Register, decoder_1_out2);
  and and_4 (and_4_out, Write_to_Register, decoder_1_out3);
  and and_5 (and_5_out, Write_to_Register, decoder_1_out4);
  and and_6 (and_6_out, Write_to_Register, decoder_1_out5);
  and and_7 (and_7_out, Write_to_Register, decoder_1_out6);
  and and_8 (and_8_out, Write_to_Register, decoder_1_out7);
  and and_9 (and_9_out, Write_to_Register, decoder_1_out8);
  and and_10 (and_10_out, Write_to_Register, decoder_1_out9);
  and and_11 (and_11_out, Write_to_Register, decoder_1_out10);
  and and_12 (and_12_out, Write_to_Register, decoder_1_out11);
  and and_13 (and_13_out, Write_to_Register, decoder_1_out12);
  and and_14 (and_14_out, Write_to_Register, decoder_1_out13);
  and and_15 (and_15_out, Write_to_Register, decoder_1_out14);
  and and_16 (and_16_out, Write_to_Register, decoder_1_out15);
  Register #(.width(16)) R0 (.D(Data_to_Write), .en(and_1_out), .Q(R0_q), .clk(CLK));  // open: clr
  Register #(.width(16)) R1 (.D(Data_to_Write), .en(and_2_out), .Q(R1_q), .clk(CLK));  // open: clr
  Register #(.width(16)) R2 (.D(Data_to_Write), .en(and_3_out), .Q(R2_q), .clk(CLK));  // open: clr
  Register #(.width(16)) R3 (.D(Data_to_Write), .en(and_4_out), .Q(R3_q), .clk(CLK));  // open: clr
  Register #(.width(16)) R4 (.D(Data_to_Write), .en(and_5_out), .Q(R4_q), .clk(CLK));  // open: clr
  Register #(.width(16)) R5 (.D(Data_to_Write), .en(and_6_out), .Q(R5_q), .clk(CLK));  // open: clr
  Register #(.width(16)) R6 (.D(Data_to_Write), .en(and_7_out), .Q(R6_q), .clk(CLK));  // open: clr
  Register #(.width(16)) R7 (.D(Data_to_Write), .en(and_8_out), .Q(R7_q), .clk(CLK));  // open: clr
  Register #(.width(16)) R8 (.D(Data_to_Write), .en(and_9_out), .Q(R8_q), .clk(CLK));  // open: clr
  Register #(.width(16)) R9 (.D(Data_to_Write), .en(and_10_out), .Q(R9_q), .clk(CLK));  // open: clr
  Register #(.width(16)) R10 (.D(Data_to_Write), .en(and_11_out), .Q(R10_q), .clk(CLK));  // open: clr
  Register #(.width(16)) R11 (.D(Data_to_Write), .en(and_12_out), .Q(R11_q), .clk(CLK));  // open: clr
  Register #(.width(16)) R12 (.D(Data_to_Write), .en(and_13_out), .Q(R12_q), .clk(CLK));  // open: clr
  Register #(.width(16)) R13 (.D(Data_to_Write), .en(and_14_out), .Q(R13_q), .clk(CLK));  // open: clr
  Register #(.width(16)) R14 (.D(Data_to_Write), .en(and_15_out), .Q(R14_q), .clk(CLK));  // open: clr
  Register #(.width(16)) R15 (.D(Data_to_Write), .en(and_16_out), .Q(R15_q), .clk(CLK));  // open: clr
  Multiplexer #(.select(4), .width(16), .enable("false")) multiplexer_1 (
    .in0(R0_q), .in1(R1_q), .in2(R2_q), .in3(R3_q), .in4(R4_q), .in5(R5_q), .in6(R6_q), .in7(R7_q),
    .in8(R8_q), .in9(R9_q), .in10(R10_q), .in11(R11_q), .in12(R12_q), .in13(R13_q), .in14(R14_q),
    .in15(R15_q), .out(OUTPUT_A), .sel(OUTPUT_A___SELECTOR));
  Multiplexer #(.select(4), .width(16), .enable("false")) multiplexer_2 (
    .in0(R0_q), .in1(R1_q), .in2(R2_q), .in3(R3_q), .in4(R4_q), .in5(R5_q), .in6(R6_q), .in7(R7_q),
    .in8(R8_q), .in9(R9_q), .in10(R10_q), .in11(R11_q), .in12(R12_q), .in13(R13_q), .in14(R14_q),
    .in15(R15_q), .out(OUTPUT_B), .sel(OUTPUT_B___SELECTOR));
endmodule

module Full_Adder (
  input  A,
  input  B,
  input  Carry_in,
  output Result,
  output Carry_out
);

  wire and_1_out, and_2_out, or_1_out;

  and and_1 (and_1_out, A, or_1_out);
  or or_1 (or_1_out, B, Carry_in);
  xor xor_1 (Result, A, B, Carry_in);
  and and_2 (and_2_out, ~A, B, Carry_in);  // AND_Gate
  or or_2 (Carry_out, and_2_out, and_1_out);
endmodule

// ADDER
module Adder (
  input  [15:0] Number_A,
  input  [15:0] Number_B,
  output Overflow_Flag,
  output [15:0] Result
);

  wire _0th_carry_out, _1th_carry_out, _2th_carry_out, _3th_carry_out, _4th_carry_out, _5th_carry_out,
       _6th_carry_out, _7th_carry_out, _8th_carry_out, _9th_carry_out, _10th_carry_out, _11th_carry_out,
       _12th_carry_out, _13th_carry_out, _14th_carry_out;

  Full_Adder _15th (
    .A(Number_A[15]), .B(Number_B[15]), .Carry_in(_14th_carry_out), .Result(Result[15]),
    .Carry_out(Overflow_Flag));
  Full_Adder _14th (
    .A(Number_A[14]), .B(Number_B[14]), .Carry_in(_13th_carry_out), .Result(Result[14]),
    .Carry_out(_14th_carry_out));
  Full_Adder _13th (
    .A(Number_A[13]), .B(Number_B[13]), .Carry_in(_12th_carry_out), .Result(Result[13]),
    .Carry_out(_13th_carry_out));
  Full_Adder _12th (
    .A(Number_A[12]), .B(Number_B[12]), .Carry_in(_11th_carry_out), .Result(Result[12]),
    .Carry_out(_12th_carry_out));
  Full_Adder _11th (
    .A(Number_A[11]), .B(Number_B[11]), .Carry_in(_10th_carry_out), .Result(Result[11]),
    .Carry_out(_11th_carry_out));
  Full_Adder _10th (
    .A(Number_A[10]), .B(Number_B[10]), .Carry_in(_9th_carry_out), .Result(Result[10]),
    .Carry_out(_10th_carry_out));
  Full_Adder _9th (
    .A(Number_A[9]), .B(Number_B[9]), .Carry_in(_8th_carry_out), .Result(Result[9]),
    .Carry_out(_9th_carry_out));
  Full_Adder _8th (
    .A(Number_A[8]), .B(Number_B[8]), .Carry_in(_7th_carry_out), .Result(Result[8]),
    .Carry_out(_8th_carry_out));
  Full_Adder _7th (
    .A(Number_A[7]), .B(Number_B[7]), .Carry_in(_6th_carry_out), .Result(Result[7]),
    .Carry_out(_7th_carry_out));
  Full_Adder _6th (
    .A(Number_A[6]), .B(Number_B[6]), .Carry_in(_5th_carry_out), .Result(Result[6]),
    .Carry_out(_6th_carry_out));
  Full_Adder _5th (
    .A(Number_A[5]), .B(Number_B[5]), .Carry_in(_4th_carry_out), .Result(Result[5]),
    .Carry_out(_5th_carry_out));
  Full_Adder _4th (
    .A(Number_A[4]), .B(Number_B[4]), .Carry_in(_3th_carry_out), .Result(Result[4]),
    .Carry_out(_4th_carry_out));
  Full_Adder _3th (
    .A(Number_A[3]), .B(Number_B[3]), .Carry_in(_2th_carry_out), .Result(Result[3]),
    .Carry_out(_3th_carry_out));
  Full_Adder _2th (
    .A(Number_A[2]), .B(Number_B[2]), .Carry_in(_1th_carry_out), .Result(Result[2]),
    .Carry_out(_2th_carry_out));
  Full_Adder _1th (
    .A(Number_A[1]), .B(Number_B[1]), .Carry_in(_0th_carry_out), .Result(Result[1]),
    .Carry_out(_1th_carry_out));
  Full_Adder _0th (.A(Number_A[0]), .B(Number_B[0]), .Carry_in(1'b0), .Result(Result[0]), .Carry_out(_0th_carry_out));
endmodule

module ALU (
  input  [15:0] Src_A,
  input  [15:0] Src_B,
  input  [3:0] IMM,
  input  [1:0] Alu_Control,
  output [15:0] Result
);

  wire [15:0] adder_1_result, and_1_out, multiplexer_1_out;

  Multiplexer #(.width(16), .enable("false")) multiplexer_1 (
    .in0(Src_B), .in1({{13{IMM[3]}}, IMM[2:0]}), .out(multiplexer_1_out), .sel(Alu_Control[1]));
  assign and_1_out = Src_A & multiplexer_1_out;  // AND_Gate and_1, 16 bits wide
  Adder adder_1 (.Number_A(Src_A), .Number_B(multiplexer_1_out), .Result(adder_1_result));  // open: Overflow_Flag
  Multiplexer #(.width(16), .enable("false")) multiplexer_2 (
    .in0(and_1_out), .in1(adder_1_result), .out(Result), .sel(Alu_Control[0]));
endmodule

// CONTROL UNIT
module Control_Unit (
  input  [3:0] Op_Code,
  input  Clock,
  output [2:0] JumpSignal,
  output [1:0] ALUControl,
  output dataMemRead,
  output memWrite,
  output regWrite,
  output jumpCondCheck,
  output PCWrite,
  output CompareSignal,
  output PCReadSignal,
  output InstReadSignal,
  output ChangePC,
  output loadData
);

  wire and_2_out, and_3_out, and_4_out, and_5_out, and_9_out, and_10_out, and_11_out, and_12_out, or_4_out,
       S0, S0_star, S1, S1_star, S2_star;

  and and_1 (S2_star, ~PCWrite, S1, S0);  // AND_Gate
  and and_2 (and_2_out, ~PCWrite, ~S1, S0);  // AND_Gate
  and and_3 (and_3_out, ~PCWrite, S1, ~S0);  // AND_Gate
  and and_4 (and_4_out, ~PCWrite, ~S1, ~S0);  // AND_Gate
  and and_5 (and_5_out, ~PCWrite, S1, ~S0);  // AND_Gate
  and and_6 (PCReadSignal, ~PCWrite, ~S1, ~S0);  // AND_Gate
  and and_7 (InstReadSignal, ~PCWrite, ~S1, S0);  // AND_Gate
  and and_8 (loadData, ~Op_Code[3], ~Op_Code[2], ~PCWrite, S1, ~S0);  // AND_Gate
  or or_1 (S1_star, and_2_out, and_3_out);
  or or_2 (S0_star, and_4_out, and_5_out);
  Register #(.width(1)) S2Reg (.D(S2_star), .en(1'b1), .Q(PCWrite), .clk(Clock));  // open: clr
  and and_9 (and_9_out, ~Op_Code[3], ~Op_Code[2], ~PCWrite, S1, ~S0);  // AND_Gate
  and and_10 (and_10_out, ~Op_Code[3], Op_Code[2], ~Op_Code[1], Op_Code[0], ~PCWrite, S1, ~S0);  // AND_Gate
  and and_11 (and_11_out, ~Op_Code[3], Op_Code[2], Op_Code[1], Op_Code[0], ~PCWrite, S1, S0);  // AND_Gate
  and and_12 (and_12_out, Op_Code[3], ~PCWrite, S1, S0);  // AND_Gate
  Register #(.width(1)) S1Reg (.D(S1_star), .en(1'b1), .Q(S1), .clk(Clock));  // open: clr
  or or_3 (regWrite, and_9_out, and_10_out);
  or or_4 (or_4_out, and_11_out, and_12_out);
  Register #(.width(1)) S0Reg (.D(S0_star), .en(1'b1), .Q(S0), .clk(Clock));  // open: clr
  Register #(.width(1)) ZFRegister (.D(or_4_out), .en(1'b1), .Q(ChangePC), .clk(Clock));  // open: clr
  and and_13 (CompareSignal, ~Op_Code[3], Op_Code[2], ~Op_Code[1], ~Op_Code[0], ~PCWrite, S1, ~S0);  // AND_Gate
  and and_14 (dataMemRead, ~Op_Code[3], Op_Code[2], ~Op_Code[1], Op_Code[0], ~PCWrite, S1, ~S0);  // AND_Gate
  and and_15 (memWrite, ~Op_Code[3], Op_Code[2], Op_Code[1], ~Op_Code[0], ~PCWrite, S1, ~S0);  // AND_Gate

  assign ALUControl = Op_Code[1:0];
  assign jumpCondCheck = Op_Code[3];
  assign JumpSignal = Op_Code[2:0];

  // Other names for the same wires on the sheet: i0 = Op_Code[0]; i1 = Op_Code[1]; Clk = Clock; i2 = Op_Code[2];
  //   i3 = Op_Code[3]; S2 = PCWrite
endmodule

// COMPARATOR
module Comparator (
  input  ComparatorSignal,
  input  [15:0] Number_A,
  input  [15:0] Number_B,
  input  Clock,
  output ZF,
  output CF
);

  wire and_1_out, and_2_out, comparator_1_eq, comparator_1_gt, comparator_1_lt;

  Comparator_part #(.width(16)) comparator_1 (
    .a(Number_A), .b(Number_B), .gt(comparator_1_gt), .eq(comparator_1_eq), .lt(comparator_1_lt));
  and and_1 (and_1_out, ~comparator_1_gt, comparator_1_eq, ~comparator_1_lt);  // AND_Gate
  and and_2 (and_2_out, ~comparator_1_gt, ~comparator_1_eq, comparator_1_lt);  // AND_Gate
  Register #(.width(1)) ZFRegister (.D(and_1_out), .en(ComparatorSignal), .Q(ZF), .clk(Clock));  // open: clr
  Register #(.width(1)) CFRegister (.D(and_2_out), .en(ComparatorSignal), .Q(CF), .clk(Clock));  // open: clr
endmodule

// Jump Condition
module Jump_Condition_Checker (
  input  jumpCondCheck,
  input  [2:0] JumpSignal,
  input  ZF,
  input  CF,
  output JumpConditionResult
);

  wire and_1_out, and_2_out, and_3_out, and_4_out, and_5_out, and_6_out, and_7_out, and_8_out, and_9_out,
       and_10_out, and_11_out, and_12_out, JA, JAE, JB, JBE, JE, or_1_out, or_2_out;

  Decoder #(.select(3), .enable("false")) decoder_1 (
    .out0(JE), .out1(JA), .out2(JB), .out3(JBE), .out4(JAE), .sel(JumpSignal));  // open: out5, out6, out7
  and and_1 (and_1_out, ~ZF, CF);  // AND_Gate
  or or_1 (or_1_out, and_1_out, and_2_out);
  and and_2 (and_2_out, ZF, ~CF);  // AND_Gate
  and and_3 (and_3_out, ~ZF, ~CF);  // AND_Gate
  and and_4 (and_4_out, ZF, ~CF);  // AND_Gate
  and and_5 (and_5_out, ZF, ~CF);  // AND_Gate
  and and_6 (and_6_out, ~ZF, ~CF);  // AND_Gate
  and and_7 (and_7_out, ~ZF, CF);  // AND_Gate
  or or_2 (or_2_out, and_3_out, and_4_out);
  and and_8 (and_8_out, and_5_out, JE, jumpCondCheck);
  and and_9 (and_9_out, and_6_out, JA, jumpCondCheck);
  and and_10 (and_10_out, and_7_out, JB, jumpCondCheck);
  and and_11 (and_11_out, or_1_out, JBE, jumpCondCheck);
  and and_12 (and_12_out, or_2_out, JAE, jumpCondCheck);
  or or_3 (JumpConditionResult, and_8_out, and_9_out, and_10_out, and_11_out, and_12_out);

  // Other names for the same wires on the sheet: JCC = jumpCondCheck
endmodule
